// Logisim project Lab3_memory.circ as structural Verilog
module memory (
  input  in_1,
  input  in_2,
  input  in_3,
  input  in_4,
  output out_5,
  output out_6,
  output out_7,
  output out_8
);

  wire and_1_out, and_2_out, nand_1_out, nand_2_out, not_1_out, not_2_out;

  not not_1 (not_1_out, in_2);
  not not_2 (not_2_out, in_4);
  and and_1 (and_1_out, not_1_out, in_1);
  and and_2 (and_2_out, in_1, in_2);
  nand nand_1 (nand_1_out, not_2_out, in_3);
  nand nand_2 (nand_2_out, in_3, in_4);
  nor nor_1 (out_5, and_1_out, out_6);
  nor nor_2 (out_6, out_5, and_2_out);
  nand nand_3 (out_7, nand_1_out, out_8);
  nand nand_4 (out_8, out_7, nand_2_out);
endmodule

module eight_bit_register (
  input  in_1,
  input  in_2,
  input  in_3,
  input  in_4,
  input  in_5,
  input  in_6,
  input  in_7,
  input  in_8,
  input  in_9,
  input  in_10,
  output out_11,
  output out_12,
  output out_13,
  output out_14,
  output out_15,
  output out_16,
  output out_17,
  output out_18
);

  wire d_ff_1_q, d_ff_2_q, d_ff_3_q, d_ff_4_q, d_ff_5_q, d_ff_6_q, d_ff_7_q, d_ff_8_q;

  D_Flip_Flop #(.trigger("falling")) d_ff_1 (.D(in_1), .clk(in_9), .Q(d_ff_1_q));  // open: Qn, preset, reset
  D_Flip_Flop #(.trigger("falling")) d_ff_2 (.D(in_2), .clk(in_9), .Q(d_ff_2_q));  // open: Qn, preset, reset
  and and_1 (out_11, in_10, d_ff_1_q);
  and and_2 (out_12, in_10, d_ff_2_q);
  D_Flip_Flop #(.trigger("falling")) d_ff_3 (.D(in_3), .clk(in_9), .Q(d_ff_3_q));  // open: Qn, preset, reset
  and and_3 (out_13, in_10, d_ff_3_q);
  D_Flip_Flop #(.trigger("falling")) d_ff_4 (.D(in_4), .clk(in_9), .Q(d_ff_4_q));  // open: Qn, preset, reset
  and and_4 (out_14, in_10, d_ff_4_q);
  D_Flip_Flop #(.trigger("falling")) d_ff_5 (.D(in_5), .clk(in_9), .Q(d_ff_5_q));  // open: Qn, preset, reset
  and and_5 (out_15, in_10, d_ff_5_q);
  D_Flip_Flop #(.trigger("falling")) d_ff_6 (.D(in_6), .clk(in_9), .Q(d_ff_6_q));  // open: Qn, preset, reset
  and and_6 (out_16, in_10, d_ff_6_q);
  D_Flip_Flop #(.trigger("falling")) d_ff_7 (.D(in_7), .clk(in_9), .Q(d_ff_7_q));  // open: Qn, preset, reset
  D_Flip_Flop #(.trigger("falling")) d_ff_8 (.D(in_8), .clk(in_9), .Q(d_ff_8_q));  // open: Qn, preset, reset
  and and_7 (out_17, in_10, d_ff_7_q);
  and and_8 (out_18, in_10, d_ff_8_q);
endmodule

module sram (
  input  in_1,
  input  in_2,
  input  in_3,
  input  in_4,
  input  [2:0] in_5,
  output [2:0] out_6
);

  wire and_1_out, and_2_out, and_3_out, and_4_out, and_5_out, decoder_1_out0, decoder_1_out1, decoder_1_out2,
       decoder_1_out3, decoder_1_out4;
  wire [2:0] d_ff_11_q, d_ff_12_q, d_ff_13_q, d_ff_14_q, d_ff_15_q;

  Decoder #(.select(3)) decoder_1 (
    .out0(decoder_1_out0), .out1(decoder_1_out1), .out2(decoder_1_out2), .out3(decoder_1_out3),
    .out4(decoder_1_out4), .sel(in_5));  // open: out5, out6, out7, en
  and and_1 (and_1_out, decoder_1_out0, in_4);
  and and_2 (and_2_out, decoder_1_out1, in_4);
  and and_3 (and_3_out, decoder_1_out2, in_4);
  and and_4 (and_4_out, decoder_1_out3, in_4);
  and and_5 (and_5_out, decoder_1_out4, in_4);
  D_Flip_Flop d_ff_1 (.D(in_1), .clk(and_1_out), .Q(d_ff_11_q[2]));  // open: Qn, preset, reset
  D_Flip_Flop #(.trigger("falling")) d_ff_2 (.D(in_1), .clk(and_2_out), .Q(d_ff_12_q[2]));  // open: Qn, preset, reset
  D_Flip_Flop #(.trigger("falling")) d_ff_3 (.D(in_1), .clk(and_3_out), .Q(d_ff_13_q[2]));  // open: Qn, preset, reset
  D_Flip_Flop #(.trigger("falling")) d_ff_4 (.D(in_1), .clk(and_4_out), .Q(d_ff_14_q[2]));  // open: Qn, preset, reset
  D_Flip_Flop #(.trigger("falling")) d_ff_5 (.D(in_1), .clk(and_5_out), .Q(d_ff_15_q[2]));  // open: Qn, preset, reset
  D_Flip_Flop #(.trigger("falling")) d_ff_6 (.D(in_2), .clk(and_1_out), .Q(d_ff_11_q[1]));  // open: Qn, preset, reset
  D_Flip_Flop #(.trigger("falling")) d_ff_7 (.D(in_2), .clk(and_2_out), .Q(d_ff_12_q[1]));  // open: Qn, preset, reset
  D_Flip_Flop #(.trigger("falling")) d_ff_8 (.D(in_2), .clk(and_3_out), .Q(d_ff_13_q[1]));  // open: Qn, preset, reset
  D_Flip_Flop #(.trigger("falling")) d_ff_9 (.D(in_2), .clk(and_4_out), .Q(d_ff_14_q[1]));  // open: Qn, preset, reset
  D_Flip_Flop #(.trigger("falling")) d_ff_10 (.D(in_2), .clk(and_5_out), .Q(d_ff_15_q[1]));  // open: Qn, preset, reset
  D_Flip_Flop #(.trigger("falling")) d_ff_11 (.D(in_3), .clk(and_1_out), .Q(d_ff_11_q[0]));  // open: Qn, preset, reset
  D_Flip_Flop #(.trigger("falling")) d_ff_12 (.D(in_3), .clk(and_2_out), .Q(d_ff_12_q[0]));  // open: Qn, preset, reset
  D_Flip_Flop #(.trigger("falling")) d_ff_13 (.D(in_3), .clk(and_3_out), .Q(d_ff_13_q[0]));  // open: Qn, preset, reset
  D_Flip_Flop #(.trigger("falling")) d_ff_14 (.D(in_3), .clk(and_4_out), .Q(d_ff_14_q[0]));  // open: Qn, preset, reset
  D_Flip_Flop #(.trigger("falling")) d_ff_15 (.D(in_3), .clk(and_5_out), .Q(d_ff_15_q[0]));  // open: Qn, preset, reset
  Multiplexer #(.select(3), .width(3)) multiplexer_1 (
    .in0(d_ff_11_q), .in1(d_ff_12_q), .in2(d_ff_13_q), .in3(d_ff_14_q), .in4(d_ff_15_q), .out(out_6),
    .sel(in_5));  // open: in5, in6, in7
endmodule

module register_file (
  input  [7:0] in_1,
  input  in_2,
  input  [1:0] in_3,
  input  [1:0] in_4,
  input  [1:0] in_5,
  output [7:0] out_6,
  output [7:0] out_7
);

  wire and_1_out, and_2_out, and_3_out, and_4_out, decoder_1_out0, decoder_1_out1, decoder_1_out2,
       decoder_1_out3;
  wire [7:0] register_1_q, register_2_q, register_3_q, register_4_q;

  Decoder #(.select(2)) decoder_1 (
    .out0(decoder_1_out0), .out1(decoder_1_out1), .out2(decoder_1_out2), .out3(decoder_1_out3), .sel(in_4));  // open: en
  Register register_1 (.D(in_1), .clk(and_1_out), .Q(register_1_q));  // open: en, clr
  and and_1 (and_1_out, decoder_1_out0, in_2);
  Register register_2 (.D(in_1), .clk(and_2_out), .Q(register_2_q));  // open: en, clr
  and and_2 (and_2_out, decoder_1_out1, in_2);
  Register register_3 (.D(in_1), .clk(and_3_out), .Q(register_3_q));  // open: en, clr
  and and_3 (and_3_out, decoder_1_out2, in_2);
  Register register_4 (.D(in_1), .clk(and_4_out), .Q(register_4_q));  // open: en, clr
  and and_4 (and_4_out, decoder_1_out3, in_2);
  Multiplexer #(.select(2), .width(8)) multiplexer_1 (
    .in0(register_1_q), .in1(register_2_q), .in2(register_3_q), .in3(register_4_q), .out(out_6), .sel(in_3));
  Multiplexer #(.select(2), .width(8)) multiplexer_2 (
    .in0(register_1_q), .in1(register_2_q), .in2(register_3_q), .in3(register_4_q), .out(out_7), .sel(in_5));
endmodule
